# Fritzing sketch sensor (saved by Fritzing 0.8.7b)
breadboards: 1

parts:
  Part1 = Arduino Uno (Rev3)
  PIR1 = PIR sensor
  U1 = XBee
  R1 = Photocell (LDR) [package=THT]
  R2 = Resistor [tolerance=±5% resistance=220 package=THT]

nets:
  N1: Part1.A5/SCL, R1.pin_1, R2.Pin_0
  GND: Part1.GND, PIR1.GND, U1.GND, R2.Pin_1
  N2: Part1.D0/RX, U1.pin20
  N3: Part1.D1/TX, U1.pin19
  N4: Part1.D4, PIR1.SIG
  3V3: Part1.3V3, U1.VCC
  5V: Part1.5V, PIR1.VDD, R1.pin_0
